# Fritzing sketch schematics (saved by Fritzing 0.9.3b)

parts:
  Arduino_UNO_R3 = Arduino Uno (Rev3)
  Q1 = NPN-Transistor [package="TO92 [THT]"]
  R1 = Resistor [tolerance=±5% resistance=1k package=THT]
  LCD1 = LCD screen
  R2 = Trimmer Potentiometer [maximum_resistance=10kΩ package=THT]
  L1 = Inductor [package="400 mil [THT]"]
  D1 = DIODE-SCHOTTKY [package=sma-diode]
  C1 = Capacitor [part_number="100 nF" package=cap-pth-5mm]
  DS1 = DS18B20 1-Wire Temperature Sensor [part_number=DS18B20]
  H1 = polarizedheader 4pin 0.156in [package=THT]
  R3 = Resistor [tolerance=±5% resistance=1k package=THT]
  R4 = Resistor [tolerance=±5% resistance=330k package=THT]
  R5 = Resistor [tolerance=±5% resistance=100k package=THT]
  Buzzer1 = Piezo Speaker

nets:
  N1: Arduino_UNO_R3.A1, L1.pin_1, D1.C, C1.1
  N2: Arduino_UNO_R3.A5/SCL, R4.Pin_1, R5.Pin_0
  N3: Arduino_UNO_R3.D8, LCD1.RS
  N4: Arduino_UNO_R3.D9_PWM, LCD1.E
  N5: Arduino_UNO_R3.D12/MISO, Buzzer1.pin1
  N6: Arduino_UNO_R3.D13/SCK, DS1.DQ
  N7: Arduino_UNO_R3.D2, R3.Pin_0
  N8: Arduino_UNO_R3.D4, LCD1.DB4
  N9: Arduino_UNO_R3.D5_PWM, LCD1.DB5
  N10: Arduino_UNO_R3.D6_PWM, LCD1.DB6
  N11: Arduino_UNO_R3.D7, LCD1.DB7
  GND: Q1.E, LCD1.R/W, LCD1.LED-, L1.pin_0, D1.A, C1.2, DS1.GND, H1.pin4, Buzzer1.pin2
  N12: Q1.C, R1.Pin_1
  N13: R1.Pin_0, H1.pin1, R4.Pin_0
  N14: LCD1.VSS, R2.leg2
  5V: LCD1.VDD, LCD1.LED+, R2.leg1, DS1.VDD
  N15: LCD1.V0, R2.wiper

notes:
  Current sensor
  To water alarm
  Temp sensor
